# Fritzing sketch SEOLO (saved by Fritzing 1.0.2b)

parts:
  PN532 = PN532 Elechouse RFID NFC Module V3
  Arduino_NANO_ESP32 = Arduino Nano ESP32
  Stepper_Motor = 28BYJ-48 Stepper Motor [part_number=28BYJ-48]
  Driver1 = 28BYJ-48 Driver Module [part_number=ULN2003 package=THT]
  MT3608 = MT3608 Boost No usb
  TP4056 = TP4056 [chip_label=TP4056 package="DIP (Dual Inline) [THT]"]
  1000mA = LIPO-1000mAh [package=lipo-1000]
  R1 = Resistor [tolerance=±5% resistance=10k package="2010 [SMD]"]
  R2 = Resistor [tolerance=±5% resistance=10k package="2010 [SMD]"]

nets:
  GND: PN532.GND, Arduino_NANO_ESP32.Pin_14, Arduino_NANO_ESP32.Pin_19, Driver1.GND, MT3608.IN_(-), MT3608.OUT_(-), TP4056.pin3, R1.Pin_1
  N1: PN532.VCC, Arduino_NANO_ESP32.Pin_2
  N2: PN532.SDA, Arduino_NANO_ESP32.Pin_7
  N3: PN532.SCL, Arduino_NANO_ESP32.Pin_8
  N4: Arduino_NANO_ESP32.Pin_6, R1.Pin_0, R2.Pin_0
  N5: Arduino_NANO_ESP32.Pin_15, Driver1.Vmotor, MT3608.OUT_(+)
  N6: Arduino_NANO_ESP32.Pin_27, Driver1.IN4
  N7: Arduino_NANO_ESP32.Pin_28, Driver1.IN3
  N8: Arduino_NANO_ESP32.Pin_29, Driver1.IN2
  N9: Arduino_NANO_ESP32.Pin_30, Driver1.IN1
  N10: Stepper_Motor.blue-pin, Driver1.blue-pin
  N11: Stepper_Motor.pink-pin, Driver1.pink-pin
  N12: Stepper_Motor.yellow-pin, Driver1.yellow-pin
  N13: Stepper_Motor.orange-pin, Driver1.orange-pin
  N14: Stepper_Motor.red-pin, Driver1.red-pin
  N15: MT3608.IN_(+), TP4056.pin6, R2.Pin_1
  N16: TP4056.pin4, 1000mA.+
  N17: TP4056.pin5, 1000mA.-

custom parts:
  PN532 Elechouse RFID NFC Module V3: NFC is a popular technology in recent years. We often heard this work while smart phone company such as Samsung or HTC introduces their latest high-end phones. Almost all the high-end phone in the market support NFC. Near field communication (NFC) is a set of standards for smart phones and similar devices to establish radio communication with each other by touching them together or bringing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
  Arduino Nano ESP32: Arduino® Nano ESP32 smd.
  28BYJ-48 Stepper Motor: Unipolar Stepper Motor 28BYJ-48 Top coil - pink & orange Bottom coil - blue & yellow Common rail - red Connector pins: blue - pink - yellow - orange - red
  28BYJ-48 Driver Module: ULN2003 Driver Module for the 28BYJ-48 Unipolar Stepper Motor LED A - Blue wire - Bottom coil left LED B - Pink wire - Top coil left LED C - Yellow wire - Bottom coil right LED D - Orange wire - Top coil right Common rail - red Connector pins: blue - pink - yellow - orange - red Control pins - IN1 to IN4 Power pins - GND & Vmotor (5-12V) On/Off jumper (if removed, power to motor is cut).
  MT3608 Boost No usb: Chip- MT3608 / B6289 DC to DC step up, power booster module. With adjustable output voltage. Current- 2A . || Input voltage- 2V-24V || Output voltage- 5V-28V Input interface- Inversed polarity- NO. || Led indicator- No.
  TP4056: A DIP stand-in part for whatever IC you want. With 6 pins on a 300mil dual inline package (DIP) footprint.
