# Fritzing sketch wifi_check (saved by Fritzing 1.0.2b)

parts:
  BAT1 = Battery Holders [package=battcon_245mm_pth]
  R1 = Resistor [tolerance=±5% resistance=330 package="1206 [SMD]"]
  LED2 = RGB LED (com. cathode, rgb) [color="Red (633nm)" current=0.030A package="5 mm [THT]"]
  R3 = Resistor [tolerance=±5% resistance=330 package="1206 [SMD]"]
  R2 = Resistor [tolerance=±5% resistance=330 package="1206 [SMD]"]
  M2 = Arduino NANO RP2040 CONNECT with headers

nets:
  N1: BAT1.+, LED2.common_cathode, M2.GND-4, M2.GND-29
  N2: BAT1.-, M2.VIN
  N3: R1.Pin_0, LED2.red_anode
  N4: R1.Pin_1, M2.D4
  N5: LED2.green_anode, R2.Pin_0
  N6: LED2.blue_anode, R3.Pin_0
  N7: R3.Pin_1, M2.D2
  N8: R2.Pin_1, M2.D3

// code stored in the sketch: wifi+voltage.ino
#include <WiFiNINA.h>

char ssid[] = "YourNetworkSSID";      // WiFi ???? ??
char pass[] = "YourNetworkPassword";  // WiFi ???? ????

int status = WL_IDLE_STATUS;  // WiFi ??

const int batteryPin = A7;   // ??? ??? ???? ???? ?
const int redPin = 4;        // ??? LED ?
const int greenPin = 3;      // ??? LED ?
const int bluePin = 2;       // ??? LED ?

void setup() {
  // ?? LED ?? ???? ??
  pinMode(LED_BUILTIN, OUTPUT);
  // ??? LED ?? ???? ??
  pinMode(redPin, OUTPUT);
  pinMode(greenPin, OUTPUT);
  pinMode(bluePin, OUTPUT);

  // ??? ?? ??
  Serial.begin(9600);
  while (!Serial) {
    ; // ??? ??? ??? ??? ??
  }

  // WiFi ?? ???
  if (WiFi.status() == WL_NO_MODULE) {
    Serial.println("WiFi module not found!");
    while (true);
  }

  // WiFi ?? ??
  while (status != WL_CONNECTED) {
    Serial.print("Attempting to connect to SSID: ");
    Serial.println(ssid);
    status = WiFi.begin(ssid, pass); // WiFi? ??? ??

    // WiFi ?? ?? ? ??? ?? 1? ?? ? ?? ??
    delay(1000);
  }

  // WiFi? ?????? ??
  Serial.println("Connected to WiFi");
}

void loop() {
  // ??? ?? ??
  int batteryLevel = analogRead(batteryPin);
  // ??? ??? ???? ?? (0-100)
  int percentage = map(batteryLevel, 0, 1023, 0, 100);

  // ??? ??? ?? LED ?? ??
  if (percentage <= 30) {
    // 30% ??? ??: ???
    setColor(255, 0, 0); // ???
  } else if (percentage <= 70) {
    // 70% ??? ??: ???
    setColor(255, 128, 0); // ???
  } else {
    // 100% ??? ??: ???
    setColor(0, 255, 0); // ???
  }

  // ??? ?? ?? LED? ???
  if (status == WL_CONNECTED) {
    digitalWrite(LED_BUILTIN, HIGH); // LED ??
    delay(500); // 0.5? ??
    digitalWrite(LED_BUILTIN, LOW);  // LED ??
    delay(500); // 0.5? ??
  }
}

// LED ?? ?? ??
void setColor(int red, int green, int blue) {
  analogWrite(redPin, red);     // ??? ??
  analogWrite(greenPin, green); // ??? ??
  analogWrite(bluePin, blue);   // ??? ??
}
